// Logisim project nandy.circ as structural Verilog: 1 circuit, main circuit main
module main (
);

  wire [7:0] ACC_q, DX_q, DY_q, SP_q;

  Register ACC (.Q(ACC_q));  // open: D, en, clk, clr
  Register SP (.Q(SP_q));  // open: D, en, clk, clr
  Register DX (.Q(DX_q));  // open: D, en, clk, clr
  Register DY (.Q(DY_q));  // open: D, en, clk, clr
  Multiplexer #(.width(8), .enable("false")) multiplexer_1 (.in0(ACC_q), .in1(SP_q));  // open: out, sel
  Multiplexer #(.width(8), .enable("false")) multiplexer_2 (.in0(SP_q), .in1(DX_q));  // open: out, sel
  Multiplexer #(.width(8), .enable("false")) multiplexer_3 (.in0(DX_q), .in1(DY_q));  // open: out, sel
endmodule
